// Logisim project Trabalho-mata-38.circ as structural Verilog: 3 circuits, main circuit ULA
module main (
  input  [7:0] \input ,
  input  [3:0] OP,
  input  [3:0] Rs1,
  input  [3:0] Rs2,
  output [7:0] OUT,
  output R0
);

  wire Clock_out, rw_ctl_out;
  wire [3:0] regs_1_rx, regs_1_ry;
  wire [7:0] bit_extender_1_out, bit_extender_2_out;

  Button Clock (.out(Clock_out));
  assign bit_extender_1_out = {{4{1'b0}}, regs_1_rx};  // Bit_Extender bit_extender_1
  assign bit_extender_2_out = {{4{1'b0}}, regs_1_ry};  // Bit_Extender bit_extender_2
  Clock rw_ctl (.out(rw_ctl_out));
  ULA ula_1 (.Ix(bit_extender_1_out), .Iy(bit_extender_2_out), .OUT(OUT), .OP(OP));
  REGs regs_1 (
    .Rx(regs_1_rx), .Ry(regs_1_ry), .clk(Clock_out), .Rin(\input [3:0]), .rw_ctl(rw_ctl_out),
    .Rd(\input [7:4]), .Rs2(Rs2), .Rs1(Rs1), .R0(R0));

  // Notes on the sheet:
  //   0011 ADIÇÃO
  //   0110 DIVISÃO
  //   0111 IGUAL 
  //   1000 MENOR
  //   0000 AND (BIT A BIT)
  //   0001 OR (BIT A BIT)
  //   0010 NÃO LÓGICO
  //   0100 SUBTRAÇÃO
  //   0101 MULTIPLICAÇÃO
  //   1001MENOR OU IGUAL
endmodule

module ULA (
  input  [7:0] Ix,
  input  [7:0] Iy,
  input  [3:0] OP,
  output [7:0] OUT
);

  wire comparator_1_eq, comparator_1_lt, not_1_out, or_2_out, or_3_out;
  wire [7:0] adder_1_out, and_1_out, bit_extender_1_out, bit_extender_2_out, bit_extender_3_out,
       bit_extender_4_out, divider_1_out, multiplier_1_out, or_1_out, subtractor_1_out;

  assign and_1_out = Ix & Iy;  // AND_Gate and_1, 8 bits wide
  assign or_1_out = Ix | Iy;  // OR_Gate or_1, 8 bits wide
  or or_2 (or_2_out, Ix[0], Ix[1], Ix[2], Ix[3], Ix[4], Ix[5], Ix[6], Ix[7]);
  Adder adder_1 (.a(Ix), .b(Iy), .out(adder_1_out));  // open: cin, cout
  Subtractor subtractor_1 (.a(Ix), .b(Iy), .out(subtractor_1_out));  // open: bin, bout
  Multiplier multiplier_1 (.a(Ix), .b(Iy), .out(multiplier_1_out));  // open: cin, cout
  Divider divider_1 (.a(Ix), .b(Iy), .out(divider_1_out));  // open: upper, rem
  Comparator comparator_1 (.a(Ix), .b(Iy), .eq(comparator_1_eq), .lt(comparator_1_lt));  // open: gt
  assign bit_extender_1_out = {{7{1'b0}}, not_1_out};  // Bit_Extender bit_extender_1
  not not_1 (not_1_out, or_2_out);
  assign bit_extender_2_out = {{7{1'b0}}, comparator_1_eq};  // Bit_Extender bit_extender_2
  assign bit_extender_3_out = {{7{1'b0}}, comparator_1_lt};  // Bit_Extender bit_extender_3
  or or_3 (or_3_out, comparator_1_lt, comparator_1_eq);
  Multiplexer #(.select(4), .width(8)) multiplexer_1 (
    .in0(and_1_out), .in1(or_1_out), .in2(bit_extender_1_out), .in3(adder_1_out), .in4(subtractor_1_out),
    .in5(multiplier_1_out), .in6(divider_1_out), .in7(bit_extender_2_out), .in8(bit_extender_3_out),
    .in9(bit_extender_4_out), .out(OUT), .sel(OP));  // open: in10, in11, in12, in13, in14, in15, en
  assign bit_extender_4_out = {{7{1'b0}}, or_3_out};  // Bit_Extender bit_extender_4
endmodule

module REGs (
  input  [3:0] Rs1,
  input  [3:0] Rs2,
  input  clk,
  input  [3:0] Rd,
  input  [3:0] Rin,
  input  rw_ctl,
  output [3:0] Rx,
  output [3:0] Ry,
  output R0
);

  wire demultiplexer_1_out0, demultiplexer_1_out1, demultiplexer_1_out2, demultiplexer_1_out3,
       demultiplexer_1_out4, demultiplexer_1_out5, demultiplexer_1_out6, demultiplexer_1_out7,
       demultiplexer_1_out8, demultiplexer_1_out9, demultiplexer_1_out10, demultiplexer_1_out11,
       demultiplexer_1_out12, demultiplexer_1_out13, demultiplexer_1_out14, demultiplexer_1_out15, or_1_out;
  wire [3:0] bit_extender_1_out, R0_q, R1_q, R2_q, R3_q, R4_q, R5_q, R6_q, R7_q, R8_q, R9_q, R10_q, R11_q,
       R12_q, R13_q, R14_q, R15_q;

  Demultiplexer #(.select(4)) demultiplexer_1 (
    .out0(demultiplexer_1_out0), .out1(demultiplexer_1_out1), .out2(demultiplexer_1_out2),
    .out3(demultiplexer_1_out3), .out4(demultiplexer_1_out4), .out5(demultiplexer_1_out5),
    .out6(demultiplexer_1_out6), .out7(demultiplexer_1_out7), .out8(demultiplexer_1_out8),
    .out9(demultiplexer_1_out9), .out10(demultiplexer_1_out10), .out11(demultiplexer_1_out11),
    .out12(demultiplexer_1_out12), .out13(demultiplexer_1_out13), .out14(demultiplexer_1_out14),
    .out15(demultiplexer_1_out15), .in(clk), .sel(Rd));  // open: en
  Multiplexer #(.select(4), .width(4)) multiplexer_1 (
    .in0(R0_q), .in1(R1_q), .in2(R2_q), .in3(R3_q), .in4(R4_q), .in5(R5_q), .in6(R6_q), .in7(R7_q),
    .in8(R8_q), .in9(R9_q), .in10(R10_q), .in11(R11_q), .in12(R12_q), .in13(R13_q), .in14(R14_q),
    .in15(R15_q), .out(Rx), .sel(Rs1));  // open: en
  Multiplexer #(.select(4), .width(4)) multiplexer_2 (
    .in0(R0_q), .in1(R1_q), .in2(R2_q), .in3(R3_q), .in4(R4_q), .in5(R5_q), .in6(R6_q), .in7(R7_q),
    .in8(R8_q), .in9(R9_q), .in10(R10_q), .in11(R11_q), .in12(R12_q), .in13(R13_q), .in14(R14_q),
    .in15(R15_q), .out(Ry), .sel(Rs2));  // open: en
  or or_1 (or_1_out, Rin[0], Rin[1], Rin[2], Rin[3]);
  assign bit_extender_1_out = {{3{1'b0}}, or_1_out};  // Bit_Extender bit_extender_1
  Register #(.width(4)) u_R0 (.D(bit_extender_1_out), .Q(R0_q), .clk(demultiplexer_1_out0));  // open: en, clr
  Register #(.width(4)) R8 (.D(Rin), .Q(R8_q), .clk(demultiplexer_1_out8));  // open: en, clr
  Register #(.width(4)) R1 (.D(Rin), .Q(R1_q), .clk(demultiplexer_1_out1));  // open: en, clr
  Register #(.width(4)) R9 (.D(Rin), .Q(R9_q), .clk(demultiplexer_1_out9));  // open: en, clr
  Register #(.width(4)) R2 (.D(Rin), .Q(R2_q), .clk(demultiplexer_1_out2));  // open: en, clr
  Register #(.width(4)) R10 (.D(Rin), .Q(R10_q), .clk(demultiplexer_1_out10));  // open: en, clr
  Register #(.width(4)) R3 (.D(Rin), .Q(R3_q), .clk(demultiplexer_1_out3));  // open: en, clr
  Register #(.width(4)) R11 (.D(Rin), .Q(R11_q), .clk(demultiplexer_1_out11));  // open: en, clr
  Register #(.width(4)) R4 (.D(Rin), .Q(R4_q), .clk(demultiplexer_1_out4));  // open: en, clr
  Register #(.width(4)) R12 (.D(Rin), .Q(R12_q), .clk(demultiplexer_1_out12));  // open: en, clr
  Register #(.width(4)) R5 (.D(Rin), .Q(R5_q), .clk(demultiplexer_1_out5));  // open: en, clr
  Register #(.width(4)) R13 (.D(Rin), .Q(R13_q), .clk(demultiplexer_1_out13));  // open: en, clr
  Register #(.width(4)) R6 (.D(Rin), .Q(R6_q), .clk(demultiplexer_1_out6));  // open: en, clr
  Register #(.width(4)) R14 (.D(Rin), .Q(R14_q), .clk(demultiplexer_1_out14));  // open: en, clr
  Register #(.width(4)) R7 (.D(Rin), .Q(R7_q), .clk(demultiplexer_1_out7));  // open: en, clr
  Register #(.width(4)) R15 (.D(Rin), .Q(R15_q), .clk(demultiplexer_1_out15));  // open: en, clr
  Bit_Extender #(.in_width(4), .out_width(1)) bit_extender_2 (.in(R0_q), .out(R0));
endmodule
